// Logisim project RISC_CPU.circ as structural Verilog: 6 circuits, main circuit main
module main (
  output halt
);

  wire CLK, jtag_uart_1_kbd_clr, jtag_uart_1_kbd_oe, jtag_uart_1_tty_clr, jtag_uart_1_tty_w,
       keyboard_1_avail, logicunit_1_bus_en, logicunit_1_bus_rw, logicunit_1_gp_m2_oe, logicunit_1_gp_m3_we,
       RST;
  wire [1:0] logicunit_1_mem_le;
  wire [2:0] logicunit_1_funct3;
  wire [4:0] logicunit_1_gp_a;
  wire [6:0] jtag_uart_1_tty_d, keyboard_1_data;
  wire [31:0] alu_1_c, logicunit_1_addr, logicunit_1_alu_a, logicunit_1_alu_b, logicunit_1_gp_dout,
       memory_1_d_out;

  Memory memory_1 (
    .ADDR(logicunit_1_addr), .EN(logicunit_1_bus_en), .RW(logicunit_1_bus_rw), .LE(logicunit_1_mem_le),
    .D_in(memory_1_d_out), .CLK(CLK), .D_out(memory_1_d_out));
  Keyboard #(.trigger("falling")) keyboard_1 (
    .clk(CLK), .re(jtag_uart_1_kbd_oe), .clr(jtag_uart_1_kbd_clr), .avail(keyboard_1_avail),
    .data(keyboard_1_data));
  Clock clock_1 (.out(CLK));
  TTY #(.cols(80), .rows(24), .trigger("falling")) tty_1 (
    .data(jtag_uart_1_tty_d), .clk(CLK), .we(jtag_uart_1_tty_w), .clr(jtag_uart_1_tty_clr));
  JTAG_UART jtag_uart_1 (
    .RW(logicunit_1_bus_rw), .EN(logicunit_1_bus_en), .LE(logicunit_1_mem_le), .ADDR(logicunit_1_addr),
    .KBD_DA(keyboard_1_avail), .KBD_D(keyboard_1_data), .CLK(CLK), .RST(RST), .D_in(memory_1_d_out),
    .D_out(memory_1_d_out), .TTY_CLR(jtag_uart_1_tty_clr), .KBD_CLR(jtag_uart_1_kbd_clr),
    .TTY_D(jtag_uart_1_tty_d), .TTY_W(jtag_uart_1_tty_w), .KBD_OE(jtag_uart_1_kbd_oe));
  // Probe on logicunit_1_addr
  // Probe on memory_1_d_out
  // Probe on logicunit_1_funct3
  LogicUnit logicunit_1 (
    .CLK(CLK), .Din(memory_1_d_out), .RST(RST), .gp_din(logicunit_1_gp_dout), .ALU_c(alu_1_c),
    .MEM_LE(logicunit_1_mem_le), .gp_M3_WE(logicunit_1_gp_m3_we), .gp_M2_OE(logicunit_1_gp_m2_oe),
    .gp_dout(logicunit_1_gp_dout), .ALU_a(logicunit_1_alu_a), .ALU_b(logicunit_1_alu_b),
    .gp_A(logicunit_1_gp_a), .funct3(logicunit_1_funct3), .halt(halt), .Addr(logicunit_1_addr),
    .Dout(memory_1_d_out), .BUS_EN(logicunit_1_bus_en), .BUS_RW(logicunit_1_bus_rw));
  // Probe on logicunit_1_gp_a
  // Probe on logicunit_1_alu_a
  // Probe on logicunit_1_alu_b
  // Probe on alu_1_c
  // Probe on logicunit_1_gp_dout
  ALU alu_1 (
    .a(logicunit_1_alu_a), .b(logicunit_1_alu_b), .funct3(logicunit_1_funct3), .CLK(CLK), .RST(RST),
    .c(alu_1_c));
  Registers registers_1 (
    .ADDR(logicunit_1_gp_a), .WE(logicunit_1_gp_m3_we), .OE(logicunit_1_gp_m2_oe),
    .D_in(logicunit_1_gp_dout), .RST(RST), .CLK(CLK), .D_out(logicunit_1_gp_dout));

  // Notes on the sheet:
  //   69
  //   108->114
  //   39
endmodule

module ALU (
  input  [2:0] funct3,
  input  [31:0] a,
  input  [31:0] b,
  input  CLK,
  input  RST,
  output [31:0] c
);

  wire comparator_1_lt, comparator_2_lt;
  wire [31:0] adder_1_out, and_1_out, bit_extender_1_out, bit_extender_2_out, multiplexer_1_out,
       multiplexer_2_out, or_1_out, shifter_1_out, shifter_2_out, shifter_3_out, xor_1_out;

  Adder #(.width(32)) adder_1 (.a(a), .b(b), .out(adder_1_out));  // open: cin, cout
  Comparator #(.width(32)) comparator_1 (.a(a), .b(b), .lt(comparator_1_lt));  // open: gt, eq
  Comparator #(.mode("unsigned"), .width(32)) comparator_2 (.a(a), .b(b), .lt(comparator_2_lt));  // open: gt, eq
  assign and_1_out = a & b;  // AND_Gate and_1, 32 bits wide
  assign or_1_out = a | b;  // OR_Gate or_1, 32 bits wide
  assign xor_1_out = a ^ b;  // XOR_Gate xor_1, 32 bits wide
  Shifter #(.width(32)) shifter_1 (.in(a), .\dist (b[4:0]), .out(shifter_1_out));
  Shifter #(.shift("lr"), .width(32)) shifter_2 (.in(a), .\dist (b[4:0]), .out(shifter_2_out));
  Shifter #(.shift("ar"), .width(32)) shifter_3 (.in(a), .\dist (b[4:0]), .out(shifter_3_out));
  assign bit_extender_1_out = {{31{1'b0}}, comparator_1_lt};  // Bit_Extender bit_extender_1
  assign bit_extender_2_out = {{31{1'b0}}, comparator_2_lt};  // Bit_Extender bit_extender_2
  // Probe on shifter_1_out
  Multiplexer #(.select(2), .width(32)) multiplexer_1 (
    .in0(shifter_2_out), .in1(shifter_3_out), .out(multiplexer_1_out), .sel(b[11:10]));  // open: in2, in3
  Multiplexer #(.select(3), .width(32)) multiplexer_2 (
    .in0(adder_1_out), .in1(shifter_1_out), .in2(bit_extender_1_out), .in3(bit_extender_2_out),
    .in4(xor_1_out), .in5(multiplexer_1_out), .in6(or_1_out), .in7(and_1_out), .out(multiplexer_2_out),
    .sel(funct3));
  Register #(.width(32)) ACC (.D(multiplexer_2_out), .en(1'b1), .clk(CLK), .Q(c), .clr(RST));
endmodule

module LogicUnit (
  input  [31:0] ALU_c,
  input  RST,
  input  CLK,
  input  [31:0] Din,
  input  [31:0] gp_din,
  output [2:0] funct3,
  output [31:0] Addr,
  output [31:0] ALU_a,
  output [31:0] ALU_b,
  output [4:0] gp_A,
  output gp_M3_WE,
  output gp_M2_OE,
  output [1:0] MEM_LE,
  output [31:0] Dout,
  output [31:0] gp_dout,
  output BUS_EN,
  output BUS_RW,
  output halt
);

  wire ALU_a_s, ALU_add, ALU_b_s, and_1_out, and_2_out, and_3_out, BRA, BRANCH_WE, comparator_2_eq,
       comparator_2_gt, comparator_2_lt, comparator_3_eq, comparator_3_gt, comparator_3_lt, comparator_4_eq,
       CYC0, CYC_rst, MAR_WE, multiplexer_3_out, not_1_out, or_1_out, or_2_out, or_3_out, PC_en, PC_ld,
       rs_sel, s1_WE, s2_WE;
  wire [1:0] gp_dsel;
  wire [2:0] CYC, CYCLE_LEN_out, funct3_t, IMM_TYPE_out;
  wire [4:0] multiplexer_8_out, rd, rs1, rs2;
  wire [6:0] funct7, opcode;
  wire [31:0] bit_extender_1_out, bit_extender_2_out, bit_extender_3_out, bit_extender_4_out,
       bit_extender_5_out, bit_extender_6_out, bit_extender_7_out, bit_extender_8_out, imm, MAR_q,
       multiplexer_6_out, multiplexer_7_out, negator_1_out, PC, PC_next, r2_q, s1, s2;

  Register #(.trigger("falling"), .width(32)) INSTR (
    .D(Din), .en(CYC0), .clk(CLK), .Q({funct7, rs2, rs1, funct3_t, rd, opcode}), .clr(RST));
  PLA #(.in_width(10), .out_width(18), .\table ("0000011001 000011000010011010 # 1 LOAD\n0000011010 000011010000011000 # 2 LOAD\n0000011011 001011001101011000 # 3 LOAD\n0010011001 000010000010000010 # 1 OP-IMM\n0010011010 001010000001000000 # 2 OP-IMM\n0010111001 000001000000000000 # 1 AUIPC\n0010111010 001001000001000000 # 2 AUIPC\n0011011001 000010000010000010 # 1 OP-IMM-32\n0011011010 001010000001000000 # 2 OP-IMM-32\n0100011001 000011000010000010 # 1 STORE\n0100011010 000011010010100100 # 2 STORE\n0100011011 001011000100000000 # 3 STORE\n0110011001 000110000010000010 # 1 OP\n0110011010 000110000010100100 # 2 OP\n0110011011 001110000001000000 # 3 OP\n0110111001 001000000001010000 # 1 LUI\n1100011001 000001000010000010 # 1 BRANCH\n1100011010 000001100010100100 # 2 BRANCH\n1100011011 011001100000000000 # 3 BRANCH\n1100111001 000010000010001010 # 1 JALR\n1100111010 011010000001001000 # 2 JALR\n1101111001 000001000000001000 # 1 JAL\n1101111010 011001000001001000 # 2 JAL\n1110011xxx 100000000000000000 # xxx SYSTEM\nxxxxxxx000 000000001100000001 # 0 INSTR")) OP_DECODER (
    .in({opcode, CYC}),
    .out({halt, PC_ld, PC_en, ALU_b_s, ALU_a_s, ALU_add, BRANCH_WE, MAR_WE, BUS_RW, BUS_EN, gp_M2_OE, gp_M3_WE, rs_sel, gp_dsel, s2_WE, s1_WE, CYC0}));
  Register #(.trigger("falling"), .width(32)) MAR (.D(ALU_c), .en(MAR_WE), .clk(CLK), .Q(MAR_q), .clr(RST));
  assign bit_extender_1_out = {{19{funct7[6]}}, {funct7[6], rd[0], funct7[5:0], rd[4:1], 1'b0}};  // Bit_Extender bit_extender_1
  assign bit_extender_2_out = {{11{funct7[6]}}, {funct7[6], rs1, funct3_t, rs2[0], funct7[5:0], rs2[4:1], 1'b0}};  // Bit_Extender bit_extender_2
  PLA #(.in_width(7), .out_width(3), .\table ("0000011 001 # LOAD\n0010011 001 # OP-IMM\n0010111 100 # AUIPC\n0011011 001 # OP-IMM-32\n0100011 010 # STORE\n0110011 000 # OP\n0110111 100 # LUI\n1100011 011 # BRANCH\n1100111 001 # JALR\n1101111 101 # JAL\n1110011 001 # SYSTEM")) IMM_TYPE (
    .in(opcode), .out(IMM_TYPE_out));
  PLA #(.in_width(7), .out_width(3), .\table ("0000011 100 # LOAD\n0010011 011 # OP-IMM\n0010111 011 # AUIPC\n0011011 011 # OP-IMM-32\n0000000 001 # NO INSTR\n0100011 100 # STORE\n0110011 100 # OP\n0110111 010 # LUI\n1100011 100 # BRANCH\n1100111 011 # JALR\n1101111 011 # JAL")) CYCLE_LEN (
    .in(opcode), .out(CYCLE_LEN_out));
  Multiplexer #(.width(32)) multiplexer_1 (.in0(MAR_q), .in1(PC), .out(Addr), .sel(CYC0));
  // Probe on opcode
  // Probe on rd
  // Probe on funct3_t
  // Probe on rs1
  // Probe on rs2
  // Probe on funct7
  assign bit_extender_3_out = {{20{funct7[6]}}, {funct7, rs2}};  // Bit_Extender bit_extender_3
  assign bit_extender_4_out = {{20{funct7[6]}}, {funct7, rd}};  // Bit_Extender bit_extender_4
  assign Dout = and_1_out ? s2 : 32'bz;  // Controlled_Buffer controlled_buffer_1
  and and_1 (and_1_out, BUS_EN, ~BUS_RW);  // AND_Gate
  Multiplexer #(.select(3), .width(32)) multiplexer_2 (
    .in1(bit_extender_3_out), .in2(bit_extender_4_out), .in3(bit_extender_1_out),
    .in4({funct7, rs2, rs1, funct3_t, {12{1'b0}}}), .in5(bit_extender_2_out), .out(imm), .sel(IMM_TYPE_out));  // open: in0, in6, in7
  Comparator #(.width(3)) comparator_1 (.a(CYCLE_LEN_out), .b(CYC), .eq(CYC_rst));  // open: gt, lt
  Counter #(.max('h7), .ongoal("stay"), .width(3)) CYCLE (
    .clr(or_1_out), .clk(CLK), .Q(CYC));  // open: load, up, count, D, carry
  or or_1 (or_1_out, RST, CYC_rst);
  // Probe on imm
  // Probe on s1
  // Probe on s2
  Comparator #(.width(32)) comparator_2 (
    .a(s1), .b(s2), .gt(comparator_2_gt), .eq(comparator_2_eq), .lt(comparator_2_lt));
  Comparator #(.mode("unsigned"), .width(32)) comparator_3 (
    .a(s1), .b(s2), .gt(comparator_3_gt), .eq(comparator_3_eq), .lt(comparator_3_lt));
  Register #(.trigger("falling"), .width(32)) r1 (.D(gp_din), .en(s1_WE), .clk(CLK), .Q(s1));  // open: clr
  Register #(.trigger("falling"), .width(32)) r2 (.D(gp_din), .en(s2_WE), .clk(CLK), .Q(r2_q));  // open: clr
  Comparator #(.width(17)) comparator_4 (
    .a({funct7, funct3_t, opcode}), .b(17'h8033), .eq(comparator_4_eq));  // open: gt, lt
  not not_1 (not_1_out, comparator_2_eq);
  or or_2 (or_2_out, comparator_2_gt, comparator_2_eq);
  Multiplexer #(.select(3)) multiplexer_3 (
    .in0(comparator_2_eq), .in1(not_1_out), .in2(1'b0), .in3(1'b0), .in4(comparator_2_lt), .in5(or_2_out),
    .in6(comparator_3_lt), .in7(or_3_out), .out(multiplexer_3_out), .sel(funct3_t));
  or or_3 (or_3_out, comparator_3_gt, comparator_3_eq);
  assign bit_extender_5_out = {{24{Din[7]}}, Din[7:0]};  // Bit_Extender bit_extender_5
  assign bit_extender_6_out = {{24{1'b0}}, Din[7:0]};  // Bit_Extender bit_extender_6
  assign bit_extender_7_out = {{16{Din[15]}}, Din[15:0]};  // Bit_Extender bit_extender_7
  assign bit_extender_8_out = {{16{1'b0}}, Din[15:0]};  // Bit_Extender bit_extender_8
  and and_2 (and_2_out, BRANCH_WE, multiplexer_3_out);
  Multiplexer #(.width(32)) multiplexer_4 (.in0(r2_q), .in1(negator_1_out), .out(s2), .sel(comparator_4_eq));
  Negator #(.width(32)) negator_1 (.in(r2_q), .out(negator_1_out));
  Multiplexer #(.width(2)) multiplexer_5 (.in0(funct3_t[1:0]), .in1(2'b11), .out(MEM_LE), .sel(CYC0));
  Multiplexer #(.select(3), .width(32)) multiplexer_6 (
    .in0(bit_extender_5_out), .in1(bit_extender_7_out), .in2(Din), .in4(bit_extender_6_out),
    .in5(bit_extender_8_out), .out(multiplexer_6_out), .sel(funct3_t));  // open: in3, in6, in7
  and and_3 (and_3_out, PC_ld, BRA);
  Register #(.trigger("falling"), .width(32)) u_PC (.D(multiplexer_7_out), .en(PC_en), .clk(CLK), .Q(PC), .clr(RST));
  Multiplexer #(.width(32)) multiplexer_7 (.in0(PC_next), .in1(ALU_c), .out(multiplexer_7_out), .sel(and_3_out));
  xnor xnor_1 (BRA, BRANCH_WE, and_2_out);
  // Probe on multiplexer_6_out
  Adder #(.width(32)) adder_1 (.a(32'h4), .b(PC), .out(PC_next));  // open: cin, cout
  Multiplexer #(.width(5)) multiplexer_8 (.in0(rs1), .in1(rs2), .out(multiplexer_8_out), .sel(rs_sel));
  Multiplexer #(.width(3)) multiplexer_9 (.in0(funct3_t), .in1(3'b000), .out(funct3), .sel(ALU_add));
  Multiplexer #(.width(32)) multiplexer_10 (.in0(PC), .in1(s1), .out(ALU_a), .sel(ALU_a_s));
  Multiplexer #(.width(32)) multiplexer_11 (.in0(imm), .in1(s2), .out(ALU_b), .sel(ALU_b_s));
  Multiplexer #(.width(5)) multiplexer_12 (.in0(multiplexer_8_out), .in1(rd), .out(gp_A), .sel(gp_M3_WE));
  Multiplexer #(.disabled("Z"), .enable("true"), .select(2), .width(32)) multiplexer_13 (
    .in0(ALU_c), .in1(PC_next), .in2(imm), .in3(multiplexer_6_out), .out(gp_dout), .sel(gp_dsel),
    .en(gp_M3_WE));

  // Other names for the same wires on the sheet: gp_WE = gp_M3_WE; gp_OE = gp_M2_OE; ALU_A_t[31:0] = ALU_c;
  //   D_in[31:0] = Din; x_read[31:0] = gp_din

  // Notes on the sheet:
  //   CLK: pull=up
  //   gp_din: pull=down
endmodule

module Memory (
  input  [31:0] ADDR,
  input  EN,
  input  RW,
  input  [1:0] LE,
  input  [31:0] D_in,
  input  CLK,
  output [31:0] D_out
);

  wire and_1_out, and_3_out, comparator_1_eq, comparator_2_eq, data_p1;
  wire [3:0] pla_1_out;
  wire [7:0] undriven, undriven_2, undriven_3, undriven_4, undriven_5, undriven_6, undriven_7, undriven_8;

  // ROM #(.addrWidth(24), .line("quad"), .misaligned("true")) text: pin names not known
  Controlled_Buffer #(.width(24)) controlled_buffer_1 (.in(ADDR[23:0]), .en(comparator_1_eq));  // open: out
  PLA #(.out_width(4), .\table ("00 0001\n01 0011\n10 1111\n11 0000")) pla_1 (.in(LE), .out(pla_1_out));
  Comparator comparator_1 (.a({8{1'b0}}), .b(ADDR[31:24]), .eq(comparator_1_eq));  // open: gt, lt
  assign D_out = and_1_out ? {undriven_4, undriven_3, undriven_2, undriven} : 32'bz;  // Controlled_Buffer controlled_buffer_2
  and and_1 (and_1_out, RW, EN, comparator_1_eq);
  // RAM #(.addrWidth(24), .enables("line"), .line("quad"), .misaligned("true"), .trigger("falling"), .\type ("nonvolatile")) data: pin names not known; wires that end beside it: data_p1, CLK
  Controlled_Buffer #(.width(24)) controlled_buffer_3 (.in(ADDR[23:0]), .en(comparator_2_eq));  // open: out
  and and_2 (data_p1, ~RW, EN, comparator_2_eq);  // AND_Gate
  Comparator comparator_2 (.a(8'h80), .b(ADDR[31:24]), .eq(comparator_2_eq));  // open: gt, lt
  and and_3 (and_3_out, RW, EN, comparator_2_eq);
  assign D_out = and_3_out ? {undriven_8, undriven_7, undriven_6, undriven_5} : 32'bz;  // Controlled_Buffer controlled_buffer_4

  // Notes on the sheet:
  //   RW: pull=up
  //   contents of text (hex, n*v repeats v):
  //   97 11 0 80 93 81 81 85 17 1 80 80 13 1 41 5a 3 25 1 0 93 5 41 0 13 6 0 0 ef 0 0 1 93 4 5 0 97 0 0 0
  //   67 80 0 0 97 7 0 80 83 a7 7 3 13 1 1 e6 23 2c 81 18 3 a5 47 0 23 2a 91 18 93 6 0 40 13 6 10 0 93 5 0
  //   0 37 84 69 74 b7 64 68 6f 23 2e 11 18 13 4 54 86 ef 0 50 24 93 84 54 36 13 5 1 14 ef 10 c0 2b 13 6 5
  //   0 93 5 0 0 13 5 1 14 ef 10 c0 26 97 35 0 0 17 35 0 0 93 85 45 73 13 5 85 73 ef 0 80 6f 97 7 0 80 83
  //   a7 87 fc 3 a5 87 0 ef 0 c0 33 97 7 0 80 83 a7 87 fb 93 5 0 5 13 5 1 14 3 a6 47 0 ef 0 c0 48 97 35 0
  //   0 93 7 1 c 13 8 1 10 13 7 1 8 93 6 1 4 13 6 1 0 93 85 85 70 13 5 1 14 ef 0 90 3b 83 27 1 0 63 88 87
  //   2 83 27 1 0 63 8c 97 2 3 27 1 0 b7 67 6f 72 93 87 17 26 63 e f7 2 17 35 0 0 93 5 1 0 13 5 c5 6e ef 0
  //   c0 67 6f f0 9f f5 83 47 41 0 e3 98 7 fc 13 5 0 0 ef 0 0 4 83 47 41 0 e3 94 7 fc 13 5 1 4 ef 0 c0 7b
  //   6f f0 5f f3 3 57 41 0 93 7 40 7 e3 10 f7 fc ef 0 40 0 13 1 1 ff 13 5 60 0 23 26 11 0 ef 0 d0 7f 13 5
  //   10 0 ef 30 40 3a 13 1 1 ff 23 24 81 0 23 26 11 0 93 7 0 0 13 4 5 0 63 88 7 0 93 5 0 0 97 0 0 0 e7 0
  //   0 0 83 a7 41 94 63 84 7 0 e7 80 7 0 13 5 4 0 ef 30 c0 36 83 97 c5 0 13 1 1 fe 23 2c 81 0 23 2a 91 0
  //   23 2e 11 0 23 28 21 1 23 26 31 1 13 f7 87 0 93 4 5 0 13 84 5 0 63 1a 7 12 3 a7 45 0 63 46 e0 0 3 a7
  //   5 4 63 56 e0 10 3 27 c4 2 63 2 7 10 3 a9 4 0 93 96 37 1 23 a0 4 0 83 25 4 2 63 dc 6 a 3 26 44 5 83
  //   57 c4 0 93 f7 47 0 63 8e 7 0 83 27 44 0 33 6 f6 40 83 27 44 3 63 86 7 0 83 27 4 4 33 6 f6 40 83 27
  //   c4 2 83 25 4 2 93 6 0 0 13 85 4 0 e7 80 7 0 13 7 f0 ff 83 57 c4 0 63 12 e5 2 83 a6 4 0 13 7 d0 1 63
  //   62 d7 a 37 7 40 20 13 7 17 0 33 57 d7 0 13 77 17 0 63 8 7 8 3 27 4 1 23 22 4 0 23 20 e4 0 13 97 37 1
  //   63 5c 7 0 93 7 f0 ff 63 16 f5 0 83 a7 4 0 63 94 7 0 23 2a a4 4 83 25 44 3 23 a0 24 1 63 8a 5 4 93 7
  //   44 4 63 86 f5 0 13 85 4 0 ef 10 c0 a 23 2a 4 2 6f 0 c0 3 13 6 0 0 93 6 10 0 13 85 4 0 e7 0 7 0 93 7
  //   f0 ff 13 6 5 0 e3 1c f5 f2 83 a7 4 0 e3 88 7 f2 13 7 d0 1 63 86 e7 0 13 7 60 1 63 94 e7 6 23 a0 24 1
  //   13 5 0 0 6f 0 c0 6 93 e7 7 4 93 97 7 1 93 d7 7 41 6f 0 40 5 83 a9 5 1 e3 82 9 fe 3 a9 5 0 93 f7 37 0
  //   23 a0 35 1 33 9 39 41 13 7 0 0 63 94 7 0 3 a7 45 1 23 24 e4 0 e3 50 20 fd 83 27 84 2 83 25 4 2 93 6
  //   9 0 13 86 9 0 13 85 4 0 e7 80 7 0 63 48 a0 2 83 17 c4 0 93 e7 7 4 23 16 f4 0 13 5 f0 ff 83 20 c1 1 3
  //   24 81 1 83 24 41 1 3 29 1 1 83 29 c1 0 13 1 1 2 67 80 0 0 b3 89 a9 0 33 9 a9 40 6f f0 df fa 83 a7 5
  //   1 63 8e 7 4 13 1 1 fe 23 2c 81 0 23 2e 11 0 13 4 5 0 63 c 5 0 83 27 5 2 63 98 7 0 23 26 b1 0 ef 0 c0
  //   31 83 25 c1 0 83 97 c5 0 63 8c 7 0 13 5 4 0 3 24 81 1 83 20 c1 1 13 1 1 2 6f f0 df dd 83 20 c1 1 3
  //   24 81 1 13 5 0 0 13 1 1 2 67 80 0 0 13 5 0 0 67 80 0 0 93 5 5 0 63 1e 5 0 37 6 0 80 37 5 0 80 13 6 6
  //   0 93 5 40 37 13 5 c5 0 6f 0 0 2e b7 7 0 80 3 a5 c7 5 6f f0 1f f7 93 7 10 0 63 c6 c7 0 13 5 0 0 67 80
  //   0 0 13 1 1 fe 23 2c 81 0 23 2a 91 0 23 28 21 1 23 22 51 1 23 2e 11 0 23 26 31 1 23 24 41 1 23 20 61
  //   1 93 a 5 0 13 89 5 0 93 4 6 0 13 84 6 0 63 8 5 0 83 27 5 2 63 94 7 0 ef 0 0 26 93 84 f4 ff 93 9 9 0
  //   83 27 44 0 63 94 7 4 93 5 4 0 13 85 a 0 ef 0 c0 4a 63 a 5 2 63 90 29 d 13 5 0 0 83 20 c1 1 3 24 81 1
  //   83 24 41 1 3 29 1 1 83 29 c1 0 3 2a 81 0 83 2a 41 0 3 2b 1 0 13 1 1 2 67 80 0 0 83 27 44 0 3 2b 4 0
  //   13 8a 4 0 63 f4 97 0 13 8a 7 0 13 6 a 0 93 5 a0 0 13 5 b 0 ef 0 50 3b 83 27 44 0 63 c 5 2 13 5 15 0
  //   b3 4 65 41 b3 87 97 40 23 20 a4 0 13 86 4 0 23 22 f4 0 93 5 b 0 13 85 9 0 b3 84 99 0 ef 0 90 60 23
  //   80 4 0 13 5 9 0 6f f0 df f7 b3 87 47 41 23 22 f4 0 83 27 4 0 13 85 9 0 13 6 a 0 b3 87 47 1 23 20 f4
  //   0 93 5 b 0 b3 84 44 41 ef 0 50 5d b3 89 49 1 e3 96 4 f2 23 80 9 0 6f f0 5f fc b7 7 0 80 93 6 6 0 13
  //   86 5 0 93 5 5 0 3 a5 c7 5 6f f0 1f eb 13 1 1 ff 23 24 81 0 23 26 11 0 13 4 5 0 23 16 b5 0 23 17 c5 0
  //   23 20 5 0 23 22 5 0 23 24 5 0 23 22 5 6 23 28 5 0 23 2a 5 0 23 2c 5 0 13 6 80 0 93 5 0 0 13 5 c5 5
  //   ef 0 d0 54 b7 17 0 0 93 87 7 d2 23 22 f4 2 b7 17 0 0 93 87 87 d7 23 24 f4 2 b7 17 0 0 93 87 c7 df 23
  //   26 f4 2 b7 17 0 0 93 87 47 e5 83 20 c1 0 23 20 84 2 23 28 f4 2 3 24 81 0 13 1 1 1 67 80 0 0 37 6 0
  //   80 37 5 0 80 13 6 6 0 93 5 40 37 13 5 c5 0 6f 0 0 e 83 25 45 0 13 1 1 ff b7 7 0 80 23 24 81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
endmodule

module Registers (
  input  [4:0] ADDR,
  input  WE,
  input  OE,
  input  [31:0] D_in,
  input  RST,
  input  CLK,
  output [31:0] D_out
);

  wire comparator_1_eq;
  wire [31:0] gp_registers_dout;

  RAM #(.addrWidth(5), .asyncread("true"), .clearpin("true"), .dataWidth(32), .trigger("falling")) gp_registers (
    .addr(ADDR), .we(WE), .oe(OE), .clk(CLK), .din(D_in), .dout(gp_registers_dout), .clr(RST));
  Comparator #(.mode("unsigned"), .width(5)) comparator_1 (
    .a(ADDR), .b({5{1'b0}}), .eq(comparator_1_eq));  // open: gt, lt
  Multiplexer #(.disabled("Z"), .enable("true"), .width(32)) multiplexer_1 (
    .in0(gp_registers_dout), .in1({32{1'b0}}), .out(D_out), .sel(comparator_1_eq), .en(OE));

  // Notes on the sheet:
  //   zero
  //   ra
  //   sp
  //   gp
  //   tp
  //   t0
  //   t1
  //   t2
  //   fp
  //   s1
  //   a0
  //   a1
  //   a2
  //   a3
  //   a4
  //   a5
  //   a6
  //   a7
  //   s2
  //   s3
  //   s4
  //   s5
  //   s6
  //   s7
  //   s8
  //   s9
  //   s10
  //   s11
  //   t3
  //   t4
  //   t5
  //   t6
endmodule

// JTAG UART
module JTAG_UART (
  input  [31:0] D_in,
  input  RW,
  input  EN,
  input  [1:0] LE,
  input  [31:0] ADDR,
  input  KBD_DA,
  input  [6:0] KBD_D,
  input  CLK,
  input  RST,
  output [6:0] TTY_D,
  output TTY_W,
  output KBD_OE,
  output [31:0] D_out,
  output TTY_CLR,
  output KBD_CLR
);

  wire and_1_out, and_2_out, and_3_out, comparator_1_eq, comparator_2_eq, comparator_3_eq;
  wire [7:0] bit_extender_1_out, multiplexer_1_out;
  wire [31:0] bit_extender_2_out;

  assign bit_extender_1_out = {{1{1'b0}}, KBD_D};  // Bit_Extender bit_extender_1
  Comparator #(.width(2)) comparator_1 (.a(LE), .b(2'b00), .eq(comparator_1_eq));  // open: gt, lt
  and and_1 (and_1_out, EN, comparator_1_eq, comparator_2_eq);
  Comparator #(.width(29)) comparator_2 (.a(29'h1ffffea0), .b(ADDR[31:3]), .eq(comparator_2_eq));  // open: gt, lt
  Comparator #(.width(3)) comparator_3 (.a(3'b100), .b(ADDR[2:0]), .eq(comparator_3_eq));  // open: gt, lt
  and and_2 (and_2_out, and_1_out, RW);
  assign bit_extender_2_out = {{24{1'b0}}, multiplexer_1_out};  // Bit_Extender bit_extender_2
  assign D_out = and_2_out ? bit_extender_2_out : 32'bz;  // Controlled_Buffer controlled_buffer_1
  Multiplexer #(.select(3), .width(8)) multiplexer_1 (
    .in0({8{1'b0}}), .in1({8{1'b0}}), .in2({{5{1'b0}}, {3{KBD_DA}}}), .in4(bit_extender_1_out), .in5(8'h50),
    .in6({8{1'b0}}), .in7({8{1'b0}}), .out(multiplexer_1_out), .sel(ADDR[2:0]));  // open: in3
  // Probe on multiplexer_1_out
  and and_3 (and_3_out, and_1_out, ~RW);  // AND_Gate
  and and_4 (TTY_W, and_3_out, comparator_3_eq);
  and and_5 (KBD_OE, comparator_3_eq, and_2_out);

  assign KBD_CLR = RST;
  assign TTY_CLR = RST;
  assign TTY_D = D_in[6:0];
endmodule
